# Fritzing sketch circuit (saved by Fritzing 0.9.3b)

parts:
  Arduino_Pro_Micro = Pro Micro
  Q1 = PNP-Transistor [part_number=2N7000 package="TO92 [THT]"]
  LED1 = LED - 3mm [color="Red (633nm)" package="3 mm [THT]"]
  R1 = Resistor [tolerance=±5% resistance=470 package="1206 [SMD]"]
  R2 = Resistor [tolerance=±5% resistance=1k package="1206 [SMD]"]
  S1 = Round Pushbutton

nets:
  GND: Arduino_Pro_Micro.GND, Q1.C, S1.leg0
  N1: Arduino_Pro_Micro.D15/SCLK, Q1.B, R2.Pin_1, S1.leg1
  5V: Arduino_Pro_Micro.VCC, R1.Pin_0, R2.Pin_0
  N2: Q1.E, LED1.cathode
  N3: LED1.anode, R1.Pin_1

notes:
  赤ボタンの例
  同じ回路を全てのボタンに対して作る

custom parts:
  Pro Micro: The SparkFun Pro Micro is a complete USB-based microcontoller development system, in a very small footprint, capable of implementing many types of projects. All programming can be done via the USB port.
